# Fritzing sketch shift (saved by Fritzing 0.8.3b)
breadboards: 2

parts:
  R1 = Resistor [tolerance=±5% resistance=220 package=THT]
  U1 = 74HC595 [package="DIP16 [THT]"]
  R2 = Resistor [tolerance=±5% resistance=220 package=THT]
  R3 = Resistor [tolerance=±5% resistance=220 package=THT]
  R4 = Resistor [tolerance=±5% resistance=220 package=THT]
  LED9 = LED - 5mm [color="Red (633nm)" package="5 mm [THT]"]
  LED10 = LED - 5mm [color="Red (633nm)" package="5 mm [THT]"]
  LED11 = LED - 5mm [color="Red (633nm)" package="5 mm [THT]"]
  LED12 = LED - 5mm [color="Red (633nm)" package="5 mm [THT]"]
  LED13 = LED - 5mm [color="Red (633nm)" package="5 mm [THT]"]
  LED14 = LED - 5mm [color="Red (633nm)" package="5 mm [THT]"]
  LED15 = LED - 5mm [color="Red (633nm)" package="5 mm [THT]"]
  LED16 = LED - 5mm [color="Red (633nm)" package="5 mm [THT]"]
  R5 = Resistor [tolerance=±5% resistance=220 package=THT]
  R6 = Resistor [tolerance=±5% resistance=220 package=THT]
  R7 = Resistor [tolerance=±5% resistance=220 package=THT]
  R8 = Resistor [tolerance=±5% resistance=220 package=THT]
  Parte1 = Arduino Uno (Rev3)

nets:
  N1: R1.Pin_0, LED10.anode
  N2: R1.Pin_1, U1.Q6
  N3: U1.Q1, R7.Pin_0
  N4: U1.Q2, R6.Pin_0
  N5: U1.Q3, R5.Pin_0
  N6: U1.Q4, R4.Pin_0
  N7: U1.Q5, R3.Pin_1
  N8: U1.Q7, R2.Pin_1
  GND: U1.GND, U1.OE, Parte1.GND
  VCC: U1.MR, U1.VCC, Parte1.5V
  N9: U1.SH_CP, Parte1.D6_PWM
  N10: U1.ST_CP, Parte1.D5_PWM
  N11: U1.DS, Parte1.D4
  N12: U1.Q0, R8.Pin_0
  N13: R2.Pin_0, LED9.anode
  N14: R3.Pin_0, LED11.anode
  N15: R4.Pin_1, LED12.anode
  N16: LED13.anode, R5.Pin_1
  N17: LED14.anode, R6.Pin_1
  N18: LED15.anode, R7.Pin_1
  N19: LED16.anode, R8.Pin_1

notes:
  Conectar todos los cátodos de los LED a GND.
  No se ha incluido por claridad en el esquema
  PIN COLOR FUNCION
  4 MORADO LATCH
  5 VERDE SEÑAL DE RELOJ
  6 AMARILLO DATOS
  CABLEADO 74HCD595 Shift Register
  +- salida 1 +5V -+
  +- salida 2 salida 0-+
  +- salida 3 morado, latch,4 -+
  +- salida 4 GND -+
  +- salida 5 verde, reloj,5 -+
  +- salida 6 amarillo, datos, 6 -+
  +- salida 7 GND -+
  +- GND -+
